# Fritzing sketch node (saved by Fritzing 0.9.5d)

parts:
  TTGO_LoRa_T3_1_6 = ESP32 TTGO LoRa T3_1.6
  Componente1 = Arduino Nano (Rev3.0)

nets:
  N1: TTGO_LoRa_T3_1_6.21, Componente1.A4
  GND: TTGO_LoRa_T3_1_6.22, TTGO_LoRa_T3_1_6.23, TTGO_LoRa_T3_1_6.GND, Componente1.GND, Componente1.A5

custom parts:
  ESP32 TTGO LoRa T3_1.6: LILYGO TTGO LoRa T3_1.6 Development Board. Protoboard Only.
